# Fritzing sketch friendship_bracelet (saved by Fritzing 1.0.0rc)
breadboards: 2

parts:
  Part1 = Adafruit Gemma M0 [part_number="Adafruit #3501"]
  J1 = Piezo Speaker
  S1 = Toggle Switch [package=THT]  # not connected
  Part2 = LED Sequin - Emerald Green [part_number=1756]
  Part3 = LED Sequin - Emerald Green [part_number=1756]
  Part4 = LED Sequin - Emerald Green [part_number=1756]
  LED1 = prefix0000
  LED2 = prefix0000
  LED3 = prefix0000
  LED4 = prefix0000
  Part5 = LED Sequin - Emerald Green [part_number=1756]
  S2 = Hall Sensor [part_number=WSH130 package=TO92]
  R1 = Resistor [tolerance=±5% power=0.25W resistance=15k package=THT]
  BAT2 = Battery Holders [package=battcon_245mm_pth]
  Part7 = Adafruit ADXL343 STEMMA QT [part_number="Adafrruit #4097"]
  Adafruit_MMC1 = Adafruit Triple-axis Magnetometer - MMC5603 - STEMMA QT / Qwiic [part_number=#5603]  # not connected
  Part8 = Adafruit STEMMA Audio Amp [part_number="Adafruit #5647"]  # not connected
  Part9 = Adafruit PCF8574 [part_number="Adafruit #5545"]
  Part10 = Adafruit Gemma M0 [part_number="Adafruit #3501"]
  J2 = Piezo Speaker
  LED1_2 = prefix0000
  LED2_2 = prefix0000
  LED3_2 = prefix0000
  LED4_2 = prefix0000
  S4 = Hall Sensor [part_number=WSH130 package=TO92]
  R2 = Resistor [tolerance=±5% power=0.25W resistance=15k package=THT]
  BAT3 = Battery Holders [package=battcon_245mm_pth]
  R3 = Resistor [tolerance=±5% power=0.25W resistance=330 package=THT]

nets:
  VCC: Part1.3.3V, LED1.connector1, LED2.connector1, LED3.connector1, LED4.connector1, S2.VCC, S2.OUT, R1.Pin_1, BAT2.+, Part7.VCC, Part9.VCC
  N1: Part1.D0_SDA_TX, Part7.SCL, Part9.SCL
  N2: Part1.D1_A0, R1.Pin_0
  N3: Part1.D2_SCL_RX, Part7.SDA/SDIO, Part9.SDA
  GND: Part1.GND, J1.pin1, Part2.-, Part3.-, Part4.-, LED1.connector3, LED2.connector3, LED3.connector3, LED4.connector3, Part5.-, S2.GND, BAT2.-, Part7.GND, Part9.GND
  N4: J1.pin2, Part9.P1
  N5: Part2.+, Part3.+, Part4.+, Part5.+, Part9.P3
  N6: LED1.connector2, Part9.P2
  N7: LED1.connector4, LED2.connector2
  N8: LED2.connector4, LED3.connector2
  N9: LED3.connector4, LED4.connector2
  3.3V: Part10.3.3V, S4.VCC, S4.OUT, R2.Pin_1, BAT3.+
  N10: Part10.D0_SDA_TX, R3.Pin_0
  N11: Part10.D1_A0, R2.Pin_0
  N12: Part10.D2_SCL_RX, J2.pin2
  GND_2: Part10.GND, J2.pin1, LED1_2.connector3, LED2_2.connector3, LED3_2.connector3, LED4_2.connector3, S4.GND, BAT3.-
  N13: Part10.VOUT, LED1_2.connector1, LED2_2.connector1, LED3_2.connector1, LED4_2.connector1
  N14: LED1_2.connector2, R3.Pin_1
  N15: LED1_2.connector4, LED2_2.connector2
  N16: LED2_2.connector4, LED3_2.connector2
  N17: LED3_2.connector4, LED4_2.connector2

notes:
  initial - v0.5
  v1.0

custom parts:
  Adafruit Gemma M0: The Adafruit Gemma M0 is a super small microcontroller board, with just enough built-in to create many simple projects. It may look small and cute: round, about the size of a quarter, with friendly alligator-clip sew pads. But do not be fooled! The Gemma M0 is incredibly powerful! We've taken the same form factor we used for the original ATtiny85-based Gemma and gave it an upgrade. The Gemma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
  LED Sequin - Emerald Green: Sew a little sparkle into your wearable project with an Adafruit LED Sequin. Simply connect 3 to 6VDC to the + pin and ground to the - pin, and the LED on the board will light up. You can make the LEDs fade and twinkle by using PWM.
  Hall Sensor: A Hall Sensor
  Adafruit ADXL343 STEMMA QT: Analog Devices has followed up on their popular classic, the ADXL345, with this near-drop-in-replacement, the ADXL343. Like the original, this is a triple-axis accelerometer with digital I2C and SPI interface breakout. It has a wide sensitivity range and high resolution, operating with an 10 or 13-bit internal ADC. Built-in motion detection features make tap, double-tap, activity, inactivity,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
  Adafruit Triple-axis Magnetometer - MMC5603 - STEMMA QT / Qwiic: Sense the magnetic fields surrounding us with this handy triple-axis magnetometer (compass) module. Magnetometers can sense where the strongest magnetic force is coming from, generally used to detect magnetic north, but can also be used for measuring magnetic fields. This sensor tends to be paired with a 6-DoF (degree of freedom) accelerometer/gyroscope to create a 9-DoF inertial measurement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
  Adafruit STEMMA Audio Amp: The Adafruit STEMMA Audio Amp is a super small mono amplifier is surprisingly powerful - able to deliver up to 2.5 Watts into 4-8 ohm impedance speakers. Inside the miniature chip is a class D controller, able to run from 2.0V-5.5VDC. Since the amp is a class D, its very efficient (over 90% efficient when driving an 8Ω speaker at over half a Watt) - making it perfect for portable and battery-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
  Adafruit PCF8574: Expand your project possibilities, with the Adafruit PCF8574 GPIO Expander Breakout - an affordable 8 channel I2C expander. GPIO expanders work like this: you have a board with some number of GPIO but not enough for your project - maybe you need more buttons or LEDs. You could upgrade to a board with massive number of GPIO like the Grand Central, or you could pop on one of these boards.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
